// Logisim project AdderSubtractor.circ as structural Verilog: 2 circuits, main circuit main
module main (
  input  A4,
  input  A3,
  input  A2,
  input  A1,
  input  B4,
  input  B3,
  input  B2,
  input  B1,
  input  M_0_for_add_1_for_sub_C_in_893f9042,
  output C_out_232c4d96,
  output S4,
  output S3,
  output S2,
  output S1
);

  wire xor_1_out, xor_2_out, xor_3_out, xor_4_out;

  xor xor_1 (xor_1_out, B4, M_0_for_add_1_for_sub_C_in_893f9042);
  xor xor_2 (xor_2_out, B3, M_0_for_add_1_for_sub_C_in_893f9042);
  xor xor_3 (xor_3_out, B2, M_0_for_add_1_for_sub_C_in_893f9042);
  xor xor_4 (xor_4_out, B1, M_0_for_add_1_for_sub_C_in_893f9042);
  L_7483_49b5b259 l_7483_49b5b259_1 (
    .A4(A4), .S3(S3), .A3(A3), .B3(xor_2_out), .VCC(1'b1), .S2(S2), .B2(xor_3_out), .A2(A2), .B4(xor_1_out),
    .S4(S4), .C_OUT_2f66db7d(C_out_232c4d96), .C_IN_14a8e841(M_0_for_add_1_for_sub_C_in_893f9042),
    .GND(1'b0), .B1(xor_4_out), .A1(A1), .S1(S1));
endmodule

// 7483
module L_7483_49b5b259 (
  input  A4,
  input  B4,
  input  A3,
  input  B3,
  input  C_IN_14a8e841,
  input  VCC,
  input  GND,
  input  B1,
  input  B2,
  input  A1,
  input  A2,
  output S3,
  output S4,
  output C_OUT_2f66db7d,
  output S2,
  output S1
);

  wire and_1_out, and_2_out, and_3_out, and_4_out, and_5_out, and_6_out, and_7_out, and_8_out, and_9_out,
       and_10_out, and_11_out, and_12_out, and_13_out, and_14_out, nand_1_out, nand_2_out, nand_3_out,
       nand_4_out, nor_1_out, nor_2_out, nor_3_out, nor_4_out, nor_6_out, nor_7_out, nor_8_out, not_1_out,
       not_2_out, not_3_out, not_4_out, not_5_out, not_6_out;

  nand nand_1 (nand_1_out, B4, A4);
  nor nor_1 (nor_1_out, B4, A4);
  nand nand_2 (nand_2_out, B3, A3);
  nor nor_2 (nor_2_out, B3, A3);
  nand nand_3 (nand_3_out, B2, A2);
  nor nor_3 (nor_3_out, B2, A2);
  nand nand_4 (nand_4_out, B1, A1);
  nor nor_4 (nor_4_out, B1, A1);
  and and_1 (and_1_out, nor_2_out, nand_1_out);
  not not_1 (not_1_out, nor_1_out);
  not not_2 (not_2_out, nor_2_out);
  not not_3 (not_3_out, nor_3_out);
  not not_4 (not_4_out, nor_4_out);
  not not_5 (not_5_out, not_6_out);
  and and_2 (and_2_out, nor_3_out, nand_1_out, nand_2_out);
  and and_3 (and_3_out, nor_4_out, nand_2_out);
  and and_4 (and_4_out, nand_2_out, nand_4_out);
  and and_5 (and_5_out, nand_1_out, not_1_out);
  and and_6 (and_6_out, nor_3_out, nand_2_out);
  and and_7 (and_7_out, nor_4_out, nand_2_out, nand_3_out);
  and and_8 (and_8_out, nand_2_out, nand_4_out);
  not not_6 (not_6_out, C_IN_14a8e841);
  and and_9 (and_9_out, nand_2_out, not_2_out);
  and and_10 (and_10_out, nor_4_out, nand_3_out);
  and and_11 (and_11_out, nand_3_out, nand_4_out, not_6_out);
  and and_12 (and_12_out, nand_3_out, not_3_out);
  and and_13 (and_13_out, nand_4_out, not_6_out);
  and and_14 (and_14_out, nand_4_out, not_4_out);
  nor nor_5 (C_OUT_2f66db7d, and_1_out, and_3_out);
  xor xor_1 (S4, and_5_out, nor_6_out);
  nor nor_6 (nor_6_out, nor_2_out, and_6_out, and_7_out, and_8_out);
  xor xor_2 (S3, and_9_out, nor_7_out);
  nor nor_7 (nor_7_out, nor_3_out, and_10_out, and_11_out);
  xor xor_3 (S2, and_12_out, nor_8_out);
  nor nor_8 (nor_8_out, nor_4_out, and_13_out);
  xor xor_4 (S1, and_14_out, not_5_out);
endmodule
