// Logisim project d_flip_flop.circ as structural Verilog: 3 circuits, main circuit main
module main (
  input  Clear,
  input  D,
  input  Clock,
  input  Preset,
  output Q,
  output Q_27739421
);

  L_7474_0d6b6d4d l_7474_0d6b6d4d_1 (
    .Clr1(Clear), .D1(D), .Clk1(Clock), .Preset1(Preset), .Q1(Q), .Q1_65c48e25(Q_27739421));  // open: Clr2, D2, Clk2, Preset2, Q2, Q2_5f4b1390
endmodule

// 7474
module L_7474_0d6b6d4d (
  input  Clr2,
  input  Clr1,
  input  D2,
  input  D1,
  input  Clk2,
  input  Clk1,
  input  Preset2,
  input  Preset1,
  output Q2,
  output Q1,
  output Q2_5f4b1390,
  output Q1_65c48e25
);

  // D_Flip_Flop d_flip_flop_1: pin names not known; wires that end beside it: Preset1, D1, Clk1, Clr1, Q1, Q1_65c48e25
  // D_Flip_Flop d_flip_flop_2: pin names not known; wires that end beside it: Preset2, D2, Clk2, Clr2, Q2, Q2_5f4b1390
endmodule

module D_Flip_Flop (
  input  Preset,
  input  D,
  input  Clr,
  input  in_4,
  output Q,
  output Q_NOT,
  output out_7
);

  wire CLK_out, clock_1_out, nand_1_out, nand_2_out, nand_3_out, nand_4_out, nand_5_out, nand_6_out,
       not_1_out, not_2_out;

  Clock CLK (.out(CLK_out));
  not not_1 (not_1_out, D);
  nand nand_1 (nand_1_out, D, CLK_out);
  nand nand_2 (nand_2_out, CLK_out, not_1_out);
  not not_2 (not_2_out, CLK_out);
  Clock clock_1 (.out(clock_1_out));
  D_Flip_Flop_part #(.trigger("high")) d_ff_1 (.D(in_4), .clk(clock_1_out), .Q(out_7));  // open: Qn, preset, reset
  nand nand_3 (nand_3_out, Preset, nand_1_out, nand_4_out);
  nand nand_4 (nand_4_out, nand_3_out, nand_2_out, Clr);
  nand nand_5 (nand_5_out, nand_3_out, not_2_out);
  nand nand_6 (nand_6_out, not_2_out, nand_4_out);
  nand nand_7 (Q, Preset, nand_5_out, Q_NOT);
  nand nand_8 (Q_NOT, Q, nand_6_out, Clr);
endmodule
