// Logisim project Sude_Çakmak_Lab4_HalfAdder.circ as structural Verilog: 1 circuit, main circuit main
module main (
  input  INPUT_A,
  input  INPUT_B,
  output SUM,
  output CARRY
);

  wire nand_1_out;

  xor xor_1 (SUM, INPUT_A, INPUT_B);
  nand nand_1 (nand_1_out, INPUT_A, INPUT_B);
  not not_1 (CARRY, nand_1_out);
endmodule
