// Logisim project Sude_Çakmak_Lab5_3.circ as structural Verilog: 3 circuits, main circuit main
module main (
  input  Pset,
  input  J,
  input  K,
  input  Clr,
  output Q1,
  output Q_prime_1
);

  wire Clk_out;

  Clock Clk (.out(Clk_out));
  _7476 u_7476_1 (
    .Preset1(Pset), .J1(J), .Clk1(Clk_out), .K1(K), .Clr1(Clr), .Q1(Q1), .Q1_prime(Q_prime_1));  // open: Preset2, J2, Clk2, K2, Clr2, Q2, Q2_prime
endmodule

module _7476 (
  input  Preset1,
  input  J1,
  input  Clk1,
  input  K1,
  input  Clr1,
  input  Preset2,
  input  J2,
  input  Clk2,
  input  K2,
  input  Clr2,
  output Q1,
  output Q1_prime,
  output Q2,
  output Q2_prime
);

  J_K_Flip_Flop j_k_flip_flop_1 (.Preset(Preset1), .J(J1), .Clk(Clk1), .K(K1), .Clr(Clr1), .Q(Q1), .Q_prime(Q1_prime));
  J_K_Flip_Flop j_k_flip_flop_2 (.Preset(Preset2), .J(J2), .Clk(Clk2), .K(K2), .Clr(Clr2), .Q(Q2), .Q_prime(Q2_prime));
endmodule

// JKFF
module J_K_Flip_Flop (
  input  Preset,
  input  J,
  input  Clk,
  input  K,
  input  Clr,
  output Q,
  output Q_prime
);

  wire nand_1_out, nand_2_out, nand_3_out, nand_4_out, nand_5_out, nand_6_out, not_1_out;

  nand nand_1 (nand_1_out, J, Clk);
  nand nand_2 (nand_2_out, Clk, K);
  not not_1 (not_1_out, Clk);
  nand nand_3 (nand_3_out, Preset, nand_1_out, nand_4_out);
  nand nand_4 (nand_4_out, nand_3_out, nand_2_out, Clr);
  nand nand_5 (nand_5_out, nand_3_out, not_1_out);
  nand nand_6 (nand_6_out, not_1_out, nand_4_out);
  nand nand_7 (Q, Preset, nand_5_out, Q_prime);
  nand nand_8 (Q_prime, Q, nand_6_out, Clr);
endmodule
