// Logisim project UnigIb_Latches.circ as structural Verilog
module D_Latch (
  input  D,
  input  C,
  output Q,
  output Q_NOT
);

  wire nand_1_out, nand_2_out, not_1_out;

  not not_1 (not_1_out, D);
  nand nand_1 (nand_1_out, D, C);
  nand nand_2 (nand_2_out, C, not_1_out);
  nand nand_3 (Q, nand_1_out, Q_NOT);
  nand nand_4 (Q_NOT, Q, nand_2_out);
endmodule

module SR_Latch (
  input  S,
  input  R,
  output Q,
  output Q_NOT
);

  nand nand_1 (Q, S, Q_NOT);
  nand nand_2 (Q_NOT, Q, R);
endmodule

module debounce (
  output Q,
  output Q_NOT
);

  wire not_1_out, S_out;

  Button S (.out(S_out));
  not not_1 (not_1_out, S_out);
  Pull_Resistor #(.pull(1)) pull_resistor_1 (.node(S_out));
  Pull_Resistor #(.pull(1)) pull_resistor_2 (.node(not_1_out));
  nand nand_1 (Q, S_out, Q_NOT);
  nand nand_2 (Q_NOT, Q, not_1_out);
endmodule

module D_Flip_Flop (
  input  Preset,
  input  D,
  input  Clr,
  input  in_4,
  output Q,
  output Q_NOT,
  output out_7
);

  wire CLK_out, clock_1_out, nand_1_out, nand_2_out, nand_3_out, nand_4_out, nand_5_out, nand_6_out,
       not_1_out, not_2_out;

  Clock CLK (.out(CLK_out));
  not not_1 (not_1_out, D);
  nand nand_1 (nand_1_out, D, CLK_out);
  nand nand_2 (nand_2_out, CLK_out, not_1_out);
  not not_2 (not_2_out, CLK_out);
  Clock clock_1 (.out(clock_1_out));
  D_Flip_Flop_part #(.trigger("high")) d_ff_1 (.D(in_4), .clk(clock_1_out), .Q(out_7));  // open: Qn, preset, reset
  nand nand_3 (nand_3_out, Preset, nand_1_out, nand_4_out);
  nand nand_4 (nand_4_out, nand_3_out, nand_2_out, Clr);
  nand nand_5 (nand_5_out, nand_3_out, not_2_out);
  nand nand_6 (nand_6_out, not_2_out, nand_4_out);
  nand nand_7 (Q, Preset, nand_5_out, Q_NOT);
  nand nand_8 (Q_NOT, Q, nand_6_out, Clr);
endmodule
